// Logisim project tarea1.circ as structural Verilog: 7 circuits, main circuit main
module main (
  input  T,
  input  [3:0] A,
  input  [3:0] B
);

  wire conversorhex_1_h0, conversorhex_1_h1, conversorhex_1_h2, conversorhex_1_h3, conversorhex_1_h4,
       conversorhex_1_h5, conversorhex_1_h6, conversorhex_2_h0, conversorhex_2_h1, conversorhex_2_h2,
       conversorhex_2_h3, conversorhex_2_h4, conversorhex_2_h5, conversorhex_2_h6, H0_out, H1_out, H2_out,
       H3_out, H4_out, H5_out, H6_out, not_1_out, t0_1_o0, t0_1_o1, t0_1_o2, t0_1_o3, t1_1_out_3, t1_1_out_4,
       t1_1_out_5, t1_1_out_6;

  T0 t0_1 (.in_1(A), .in_2(B), .O3(t0_1_o3), .O2(t0_1_o2), .O1(t0_1_o1), .O0(t0_1_o0));
  T1 t1_1 (.in_1(A), .in_2(B), .out_3(t1_1_out_3), .out_4(t1_1_out_4), .out_5(t1_1_out_5), .out_6(t1_1_out_6));
  not not_1 (not_1_out, T);
  conversorHEX conversorhex_1 (
    .O3(t0_1_o3), .O2(t0_1_o2), .O1(t0_1_o1), .O0(t0_1_o0), .in_3(not_1_out), .H6(conversorhex_1_h6),
    .H5(conversorhex_1_h5), .H4(conversorhex_1_h4), .H3(conversorhex_1_h3), .H2(conversorhex_1_h2),
    .H1(conversorhex_1_h1), .H0(conversorhex_1_h0));
  conversorHEX conversorhex_2 (
    .O3(t1_1_out_3), .O2(t1_1_out_4), .O1(t1_1_out_5), .O0(t1_1_out_6), .in_3(T), .H6(conversorhex_2_h6),
    .H5(conversorhex_2_h5), .H4(conversorhex_2_h4), .H3(conversorhex_2_h3), .H2(conversorhex_2_h2),
    .H1(conversorhex_2_h1), .H0(conversorhex_2_h0));
  or H6 (H6_out, conversorhex_1_h6, conversorhex_2_h6);
  or H5 (H5_out, conversorhex_1_h5, conversorhex_2_h5);
  or H4 (H4_out, conversorhex_1_h4, conversorhex_2_h4);
  or H3 (H3_out, conversorhex_1_h3, conversorhex_2_h3);
  or H2 (H2_out, conversorhex_1_h2, conversorhex_2_h2);
  or H1 (H1_out, conversorhex_1_h1, conversorhex_2_h1);
  or H0 (H0_out, conversorhex_1_h0, conversorhex_2_h0);
  LED led_1 (.in(H6_out));
  LED led_2 (.in(H1_out));
  LED led_3 (.in(H1_out));
  LED led_4 (.in(H1_out));
  LED led_5 (.in(H0_out));
  LED led_6 (.in(H0_out));
  LED led_7 (.in(H2_out));
  LED led_8 (.in(H2_out));
  LED led_9 (.in(H2_out));
  LED led_10 (.in(H3_out));
  LED led_11 (.in(H6_out));
  LED led_12 (.in(H6_out));
  LED led_13 (.in(H5_out));
  LED led_14 (.in(H5_out));
  LED led_15 (.in(H5_out));
  LED led_16 (.in(H0_out));
  LED led_17 (.in(H4_out));
  LED led_18 (.in(H4_out));
  LED led_19 (.in(H4_out));
  LED led_20 (.in(H3_out));
  LED led_21 (.in(H3_out));
endmodule

// T=0
module T0 (
  input  [3:0] in_1,
  input  [3:0] in_2,
  output O3,
  output O2,
  output O1,
  output O0
);

  wire amasb_1_out_5, amasb_2_out_5, amasb_3_out_5, amasb_4_out_5;

  amasb amasb_1 (.in_1(in_1[3]), .in_2(in_2[3]), .in_3(amasb_2_out_5), .out_4(O3), .out_5(amasb_1_out_5));
  amasb amasb_2 (.in_1(in_1[2]), .in_2(in_2[2]), .in_3(amasb_3_out_5), .out_4(O2), .out_5(amasb_2_out_5));
  amasb amasb_3 (.in_1(in_1[1]), .in_2(in_2[1]), .in_3(amasb_4_out_5), .out_4(O1), .out_5(amasb_3_out_5));
  amasb amasb_4 (.in_1(in_1[0]), .in_2(in_2[0]), .in_3(1'b0), .out_4(O0), .out_5(amasb_4_out_5));
endmodule

module amasb (
  input  in_1,
  input  in_2,
  input  in_3,
  output out_4,
  output out_5
);

  wire and_1_out, and_2_out, xor_1_out;

  xor xor_1 (xor_1_out, in_1, in_2);
  and and_1 (and_1_out, in_1, in_2);
  xor xor_2 (out_4, xor_1_out, in_3);
  and and_2 (and_2_out, xor_1_out, in_3);
  or or_1 (out_5, and_2_out, and_1_out);
endmodule

// T=1
module T1 (
  input  [3:0] in_1,
  input  [3:0] in_2,
  output out_3,
  output out_4,
  output out_5,
  output out_6
);

  f f_1 (.x(in_1[2]), .y(in_1[1]), .z(in_1[0]), .S(out_3));
  g g_1 (.in_1(in_1[3]), .in_2(in_1[2]), .in_3(in_1[1]), .in_4(in_1[0]), .out_5(out_4));
  f f_2 (.x(in_2[2]), .y(in_2[1]), .z(in_2[0]), .S(out_5));
  g g_2 (.in_1(in_2[3]), .in_2(in_2[2]), .in_3(in_2[1]), .in_4(in_2[0]), .out_5(out_6));
endmodule

module f (
  input  x,
  input  y,
  input  z,
  output S
);

  wire and_1_out, and_2_out, and_3_out, and_4_out, nor_1_out, not_1_out, not_2_out, not_3_out, not_4_out,
       not_5_out, not_6_out, or_1_out;

  not not_1 (not_1_out, x);
  not not_2 (not_2_out, y);
  not not_3 (not_3_out, y);
  not not_4 (not_4_out, z);
  not not_5 (not_5_out, x);
  not not_6 (not_6_out, z);
  and and_1 (and_1_out, x, y, z);
  and and_2 (and_2_out, not_1_out, not_2_out);
  and and_3 (and_3_out, not_3_out, not_4_out);
  and and_4 (and_4_out, not_5_out, not_6_out);
  or or_1 (or_1_out, and_1_out, and_2_out, and_3_out, and_4_out);
  nor nor_1 (nor_1_out, x, y, z);
  xor xor_1 (S, or_1_out, nor_1_out);
endmodule

module g (
  input  in_1,
  input  in_2,
  input  in_3,
  input  in_4,
  output out_5
);

  wire f_1_s;

  f f_1 (.x(in_2), .y(in_3), .z(in_4), .S(f_1_s));
  xor xor_1 (out_5, in_1, f_1_s);
endmodule

// HEX
module conversorHEX (
  input  O3,
  input  O2,
  input  in_3,
  input  O1,
  input  O0,
  output H6,
  output H5,
  output H4,
  output H3,
  output H2,
  output H1,
  output H0
);

  wire and_1_out, and_2_out, and_3_out, and_4_out, and_5_out, and_6_out, and_7_out, and_8_out, and_9_out,
       and_10_out, and_11_out, and_12_out, and_13_out, and_14_out, and_15_out, and_16_out, and_17_out,
       and_18_out, and_19_out, and_20_out, and_21_out, and_22_out, and_23_out, and_24_out, and_25_out,
       and_26_out, and_27_out, and_28_out, and_29_out, and_30_out, and_31_out, and_32_out, and_33_out,
       and_34_out, and_35_out, not_1_out, not_2_out, not_3_out, not_4_out, not_5_out, not_6_out, not_7_out,
       not_8_out, not_9_out, not_10_out, not_11_out, not_12_out, not_13_out, not_14_out, not_15_out,
       not_16_out, not_17_out, not_18_out, not_19_out, not_20_out, not_21_out, not_22_out, not_23_out,
       not_24_out, not_25_out, not_26_out, not_27_out, not_28_out, not_29_out, not_30_out, not_31_out,
       not_32_out, not_33_out, not_34_out, not_35_out, not_36_out, not_37_out, not_38_out, not_39_out,
       not_40_out, not_41_out, not_42_out, not_43_out, or_1_out, or_2_out, or_3_out, or_4_out, or_5_out,
       or_6_out, or_7_out;

  not not_1 (not_1_out, O2);
  and and_1 (and_1_out, not_1_out, not_2_out);
  not not_2 (not_2_out, O0);
  not not_3 (not_3_out, O3);
  and and_2 (and_2_out, not_3_out, O1);
  not not_4 (not_4_out, O3);
  and and_3 (and_3_out, not_4_out, O2, O0);
  and and_4 (and_4_out, O2, O1);
  and and_5 (and_5_out, O3, not_5_out, not_6_out);
  not not_5 (not_5_out, O2);
  not not_6 (not_6_out, O1);
  and and_6 (and_6_out, O3, not_7_out);
  not not_7 (not_7_out, O0);
  not not_8 (not_8_out, O3);
  and and_7 (and_7_out, not_8_out, not_9_out);
  not not_9 (not_9_out, O2);
  not not_10 (not_10_out, O3);
  not not_11 (not_11_out, O1);
  and and_8 (and_8_out, not_10_out, not_11_out, not_12_out);
  not not_12 (not_12_out, O0);
  not not_13 (not_13_out, O2);
  and and_9 (and_9_out, not_13_out, not_14_out);
  not not_14 (not_14_out, O0);
  not not_15 (not_15_out, O3);
  and and_10 (and_10_out, not_15_out, O1, O0);
  not not_16 (not_16_out, O1);
  and and_11 (and_11_out, O3, not_16_out, O0);
  not not_17 (not_17_out, O3);
  and and_12 (and_12_out, not_17_out, not_18_out);
  not not_18 (not_18_out, O1);
  not not_19 (not_19_out, O3);
  and and_13 (and_13_out, not_19_out, O0);
  not not_20 (not_20_out, O1);
  and and_14 (and_14_out, not_20_out, O0);
  not not_21 (not_21_out, O3);
  and and_15 (and_15_out, not_21_out, O2);
  and and_16 (and_16_out, O3, not_22_out);
  not not_22 (not_22_out, O2);
  not not_23 (not_23_out, O3);
  not not_24 (not_24_out, O2);
  and and_17 (and_17_out, not_23_out, not_24_out, not_25_out);
  not not_25 (not_25_out, O0);
  not not_26 (not_26_out, O2);
  and and_18 (and_18_out, not_26_out, O1, O0);
  and and_19 (and_19_out, O2, not_27_out, O0);
  not not_27 (not_27_out, O1);
  and and_20 (and_20_out, O2, O1, not_28_out);
  not not_28 (not_28_out, O0);
  and and_21 (and_21_out, O3, not_29_out);
  not not_29 (not_29_out, O1);
  not not_30 (not_30_out, O2);
  and and_22 (and_22_out, not_30_out, not_31_out);
  not not_31 (not_31_out, O0);
  and and_23 (and_23_out, O1, not_32_out);
  not not_32 (not_32_out, O0);
  and and_24 (and_24_out, O3, O1);
  and and_25 (and_25_out, O3, O2);
  not not_33 (not_33_out, O1);
  and and_26 (and_26_out, not_33_out, not_34_out);
  not not_34 (not_34_out, O0);
  not not_35 (not_35_out, O3);
  and and_27 (and_27_out, not_35_out, O2, not_36_out);
  not not_36 (not_36_out, O1);
  and and_28 (and_28_out, O2, not_37_out);
  not not_37 (not_37_out, O0);
  and and_29 (and_29_out, O3, not_38_out);
  not not_38 (not_38_out, O2);
  and and_30 (and_30_out, O3, O1);
  not not_39 (not_39_out, O2);
  and and_31 (and_31_out, not_39_out, O1);
  and and_32 (and_32_out, O1, not_40_out);
  not not_40 (not_40_out, O0);
  not not_41 (not_41_out, O3);
  and and_33 (and_33_out, not_41_out, O2, not_42_out);
  not not_42 (not_42_out, O1);
  and and_34 (and_34_out, O3, not_43_out);
  not not_43 (not_43_out, O2);
  and and_35 (and_35_out, O3, O0);
  or or_1 (or_1_out, and_7_out, and_8_out, and_9_out, and_10_out, and_11_out);
  or or_2 (or_2_out, and_12_out, and_13_out, and_14_out, and_15_out, and_16_out);
  or or_3 (or_3_out, and_17_out, and_18_out, and_19_out, and_20_out, and_21_out);
  or or_4 (or_4_out, and_22_out, and_23_out, and_24_out, and_25_out);
  or or_5 (or_5_out, and_26_out, and_27_out, and_28_out, and_29_out, and_30_out);
  or or_6 (or_6_out, and_31_out, and_32_out, and_33_out, and_34_out, and_35_out);
  or or_7 (or_7_out, and_1_out, and_2_out, and_3_out, and_4_out, and_5_out, and_6_out);
  and and_36 (H6, in_3, or_7_out);
  and and_37 (H5, in_3, or_1_out);
  and and_38 (H4, in_3, or_2_out);
  and and_39 (H3, in_3, or_3_out);
  and and_40 (H2, in_3, or_4_out);
  and and_41 (H1, in_3, or_5_out);
  and and_42 (H0, in_3, or_6_out);
endmodule
