// Logisim project tarea3.circ as structural Verilog: 8 circuits, main circuit main
module main (
  input  [1:0] M,
  input  [7:0] X,
  output S7,
  output S6,
  output S5,
  output S4,
  output S3,
  output S2,
  output S1,
  output S0
);

  wire CLK_out, not_1_out;
  wire [7:0] FF1_out_3, FF2_out_3;

  Clock CLK (.out(CLK_out));
  not not_1 (not_1_out, CLK_out);
  FF_D FF1 (.D(X), .out_3(FF1_out_3), .CLK(CLK_out));
  FF_D FF2 (.D(FF1_out_3), .out_3(FF2_out_3), .CLK(not_1_out));
  SLogic slogic_1 (.X(FF2_out_3), .P_X(FF1_out_3), .out_4({S7, S6, S5, S4, S3, S2, S1, S0}), .in_1(M));

  // Notes on the sheet:
  //   S
endmodule

// S Logic
module SLogic (
  input  [1:0] in_1,
  input  [7:0] X,
  input  [7:0] P_X,
  output [7:0] out_4
);

  wire [7:0] _10_out, _11_out, restabits_1_s, sumabits_1_s;

  sumaBits sumabits_1 (.A(X), .B(P_X), .S(sumabits_1_s));
  restaBits restabits_1 (.A(X), .B(P_X), .S(restabits_1_s));
  assign _10_out = X | P_X;  // OR_Gate _10, 8 bits wide
  assign _11_out = X & P_X;  // AND_Gate _11, 8 bits wide
  Multiplexer #(.select(2), .width(8)) multiplexer_1 (
    .in0(sumabits_1_s), .in1(restabits_1_s), .in2(_10_out), .in3(_11_out), .out(out_4), .sel(in_1));  // open: en
endmodule

module FF_D (
  input  CLK,
  input  [7:0] D,
  output [7:0] out_3
);

  D d_1 (.D(D[7]), .out_3(out_3[7]), .CLK(CLK));  // open: out_4
  D d_2 (.D(D[6]), .out_3(out_3[6]), .CLK(CLK));  // open: out_4
  D d_3 (.D(D[5]), .out_3(out_3[5]), .CLK(CLK));  // open: out_4
  D d_4 (.D(D[4]), .out_3(out_3[4]), .CLK(CLK));  // open: out_4
  D d_5 (.D(D[3]), .out_3(out_3[3]), .CLK(CLK));  // open: out_4
  D d_6 (.D(D[2]), .out_3(out_3[2]), .CLK(CLK));  // open: out_4
  D d_7 (.D(D[1]), .out_3(out_3[1]), .CLK(CLK));  // open: out_4
  D d_8 (.D(D[0]), .out_3(out_3[0]), .CLK(CLK));  // open: out_4
endmodule

module D (
  input  CLK,
  input  D,
  output out_3,
  output out_4
);

  wire and_1_out, and_2_out, not_1_out;

  not not_1 (not_1_out, D);
  and and_1 (and_1_out, CLK, not_1_out);
  and and_2 (and_2_out, CLK, D);
  SR sr_1 (.S(and_1_out), .R(and_2_out), .out_3(out_3), .out_4(out_4));
endmodule

module SR (
  input  S,
  input  R,
  output out_3,
  output out_4
);

  nor nor_1 (out_3, S, out_4);
  nor nor_2 (out_4, out_3, R);
endmodule

// 00
module sumaBits (
  input  [7:0] A,
  input  [7:0] B,
  output [7:0] S
);

  wire suma_2_s0, suma_3_s0, suma_4_s0, suma_5_s0, suma_6_s0, suma_7_s0, suma_8_s0;

  suma suma_1 (.A(A[7]), .B(B[7]), .C(suma_2_s0), .S1(S[7]));  // open: S0
  suma suma_2 (.A(A[6]), .B(B[6]), .C(suma_3_s0), .S1(S[6]), .S0(suma_2_s0));
  suma suma_3 (.A(A[5]), .B(B[5]), .C(suma_4_s0), .S1(S[5]), .S0(suma_3_s0));
  suma suma_4 (.A(A[4]), .B(B[4]), .C(suma_5_s0), .S1(S[4]), .S0(suma_4_s0));
  suma suma_5 (.A(A[3]), .B(B[3]), .C(suma_6_s0), .S1(S[3]), .S0(suma_5_s0));
  suma suma_6 (.A(A[2]), .B(B[2]), .C(suma_7_s0), .S1(S[2]), .S0(suma_6_s0));
  suma suma_7 (.A(A[1]), .B(B[1]), .C(suma_8_s0), .S1(S[1]), .S0(suma_7_s0));
  suma suma_8 (.A(A[0]), .B(B[0]), .C(1'b0), .S1(S[0]), .S0(suma_8_s0));
endmodule

// 01
module restaBits (
  input  [7:0] A,
  input  [7:0] B,
  output [7:0] S
);

  wire suma_2_s0, suma_3_s0, suma_4_s0, suma_5_s0, suma_6_s0, suma_7_s0, suma_8_s0;
  wire [7:0] not_1_out;

  assign not_1_out = ~B;  // NOT_Gate not_1, 8 bits wide
  suma suma_1 (.A(A[7]), .B(not_1_out[7]), .C(suma_2_s0), .S1(S[7]));  // open: S0
  suma suma_2 (.A(A[6]), .B(not_1_out[6]), .C(suma_3_s0), .S1(S[6]), .S0(suma_2_s0));
  suma suma_3 (.A(A[5]), .B(not_1_out[5]), .C(suma_4_s0), .S1(S[5]), .S0(suma_3_s0));
  suma suma_4 (.A(A[4]), .B(not_1_out[4]), .C(suma_5_s0), .S1(S[4]), .S0(suma_4_s0));
  suma suma_5 (.A(A[3]), .B(not_1_out[3]), .C(suma_6_s0), .S1(S[3]), .S0(suma_5_s0));
  suma suma_6 (.A(A[2]), .B(not_1_out[2]), .C(suma_7_s0), .S1(S[2]), .S0(suma_6_s0));
  suma suma_7 (.A(A[1]), .B(not_1_out[1]), .C(suma_8_s0), .S1(S[1]), .S0(suma_7_s0));
  suma suma_8 (.A(A[0]), .B(not_1_out[0]), .C(1'b1), .S1(S[0]), .S0(suma_8_s0));
endmodule

module suma (
  input  A,
  input  B,
  input  C,
  output S1,
  output S0
);

  wire and_1_out, and_2_out, and_3_out, and_4_out, and_5_out, and_6_out, and_7_out, not_1_out, not_2_out,
       not_3_out, not_4_out, not_5_out, not_6_out;

  not not_1 (not_1_out, A);
  not not_2 (not_2_out, B);
  not not_3 (not_3_out, A);
  not not_4 (not_4_out, C);
  not not_5 (not_5_out, B);
  not not_6 (not_6_out, C);
  and and_1 (and_1_out, B, C);
  and and_2 (and_2_out, A, C);
  and and_3 (and_3_out, A, B);
  and and_4 (and_4_out, not_1_out, not_2_out, C);
  and and_5 (and_5_out, not_3_out, B, not_4_out);
  and and_6 (and_6_out, A, not_5_out, not_6_out);
  and and_7 (and_7_out, A, B, C);
  or or_1 (S0, and_1_out, and_2_out, and_3_out);
  or or_2 (S1, and_4_out, and_5_out, and_6_out, and_7_out);
endmodule
